// Logisim project cpu.circ as structural Verilog: 1 circuit, main circuit cpu
module cpu (
  input  clk,
  input  [31:0] INSTRUCTION,
  input  [31:0] MEM_READ_DATA,
  output [31:0] MEM_WRITE_ADDRESS,
  output [31:0] PROGRAM_COUNTER,
  output [31:0] ra,
  output [31:0] sp,
  output [31:0] t0,
  output [31:0] t1,
  output [31:0] t2,
  output [31:0] s0,
  output [31:0] s1,
  output [31:0] a0,
  output [31:0] tohost,
  output [3:0] MEM_WRITE_ENABLE,
  output [31:0] MEM_WRITE_DATA
);

  wire RegWEn;
  wire [2:0] control_logic_1_immsel;
  wire [3:0] control_logic_1_alusel;
  wire [31:0] adder_1_out, imm_gen_1_imm, regfile_1_read_data_1, Result;

  Adder #(.width(32)) adder_1 (.a(PROGRAM_COUNTER), .b(32'h4), .out(adder_1_out));  // open: cin, cout
  Register #(.width(32)) PC (.D(adder_1_out), .clk(clk), .Q(PROGRAM_COUNTER));  // open: en, clr
  control_logic control_logic_1 (
    .RegWEn(RegWEn), .ImmSel(control_logic_1_immsel), .ALUSel(control_logic_1_alusel), .inst(INSTRUCTION));  // open: CSRWen, out_15, PCSel, BrUn, ASel, BSel, MemRW, WBSel, CSRSel, BrEq, BrLt
  regfile regfile_1 (
    .rs1(INSTRUCTION[19:15]), .rd(INSTRUCTION[11:7]), .Write_Data(Result), .RegWEn(RegWEn), .clk(clk),
    .ra(ra), .sp(sp), .t0(t0), .t1(t1), .t2(t2), .s0(s0), .s1(s1), .a0(a0),
    .Read_Data_1(regfile_1_read_data_1));  // open: rs2, Read_Data_2
  imm_gen imm_gen_1 (.inst(INSTRUCTION), .ImmSel(control_logic_1_immsel), .imm(imm_gen_1_imm));
  alu alu_1 (.Result(Result), .A(regfile_1_read_data_1), .B(imm_gen_1_imm), .ALUSel(control_logic_1_alusel));
  // branch_comp branch_comp_1: pin names not known
  csr csr_1 (.tohost(tohost));  // open: CSR_address, CSR_din, CSR_WE, clk

  // Other names for the same wires on the sheet: rd[4:0] = INSTRUCTION[11:7]

  // Notes on the sheet:
  //   Output to IMEM
  //   IMEM (do **NOT** move this)
  //   Inputs from IMEM
  //   It is OK to move the PC, RegFile, ALU, MEM, Branch Comp, Imm Gen, and Control Logic to wherever is most convenient for you when constructing your CPU, and to delete this text
  //   Inputs/Outputs for testing. Do **NOT** move these.
  //   Outputs To DMEM
  //   DMEM (do **NOT** move this)
  //   Inputs From DMEM
endmodule
